# Fritzing sketch RemoteStepperPCB_ProfV1_3 (saved by Fritzing 0.9.1b)
circuit board: 3.08951cm x 2.09106cm
breadboards: 1

parts:
  U3 = ATTINY45 [package=dip]
  XTAL3 = Crystal [frequency="16 Mhz" package=THT]
  J8 = double row female pin header, 8 pins [form="♀ (female)"]
  J9 = female pin header, 4 pins [form="♀ (female)"]
  J11 = female pin header, 8 pins [form="♀ (female)"]
  J10 = female pin header, 8 pins [form="♀ (female)"]

nets:
  N1: U3.PB3(ADC3), XTAL3.pin_0
  N2: U3.PB4(ADC2), XTAL3.pin_1
  N3: U3.GND, J8.pin1, J8.pin8, J10.pin1, J10.pin7
  N4: U3.PB0(MOSI), J11.pin2
  N5: U3.PB1(MISO), J11.pin1
  N6: U3.PB2(SCK_ADC1), J8.pin2, J8.pin7
  N7: U3.VCC, J8.pin3, J8.pin6, J10.pin2
  N8: J8.pin4, J8.pin5, J10.pin8
  N9: J9.pin1, J10.pin3
  N10: J9.pin2, J10.pin4
  N11: J9.pin3, J10.pin5
  N12: J9.pin4, J10.pin6
  N13: J11.pin3, J11.pin4
