# Fritzing sketch LEDARv5 (saved by Fritzing 0.9.2b)
circuit board: 2.32cm x 2.32cm
breadboards: 1

parts:
  S1 = Toggle Switch [package=THT]
  16Mhz = Crystal [frequency="16 Mhz" package=THT]
  TX = LED - 5mm [color="Red (633nm)" package="5 mm [THT]"]
  R1 = Resistor [tolerance=±5% resistance=220 package=THT]
  RX = LED - 5mm [color="Red (633nm)" package="5 mm [THT]"]
  R2 = Resistor [tolerance=±5% resistance=220 package=THT]
  ATtiny85 = attiny85 [package=dip]

nets:
  N1: S1.L1, TX.cathode, RX.cathode, R2.Pin_0, ATtiny85.Pin_4
  N2: S1.COM, ATtiny85.Pin_8
  N3: S1.L2, ATtiny85.Pin_6
  N4: 16Mhz.pin_0, ATtiny85.Pin_3
  N5: 16Mhz.pin_1, ATtiny85.Pin_2
  N6: TX.anode, R1.Pin_0
  N7: R1.Pin_1, ATtiny85.Pin_5
  N8: RX.anode, R2.Pin_1, ATtiny85.Pin_7

notes:
  GND
  PJON DISTANCE & LIGHT SENSOR
  Giovanni Blu Mitolo 2017
  5v
  PJON
  TX resistor
  RX resistor
  RX DIODE
  TX DIODE
  LEDAR
