# Fritzing sketch SurrogateViaEthernet (saved by Fritzing 0.9.3b)

parts:
  Part1 = Arduino Uno (Rev3) - ICSP  # not connected
  Part3 = Arduino Uno (Rev3) - ICSP
  Part4 = Arduino Ethernet Shield (Rev3)
  Part5 = Arduino Uno (Rev3) - ICSP  # not connected
  Part6 = Arduino Ethernet Shield (Rev3)  # not connected

nets:
  N1: Part3.D12/MISO, Part4.D7
  5V: Part3.5V, Part4.5V
  GND: Part3.GND, Part4.GND

notes:
  Surrogate on an Uno with Ethernet Shield
  SoftwareBitBang BlinkWithResponse Receiver example
  Surrogate and RemoteWorker setup
  Parttake via Ethernet in a SoftwareBitBang bus
  Device 45 on an ETCP bus sends a BLINK packet to device 44 as if it were on the same bus.
  For each packet coming in return from devices 44 it will print BLINK to the serial port. (LED is not available when Ethernet shield is mounted.)
  This device can be placed in another location than the SWBB bus as long as it is reachable through Ethernet. It may be separated by routers or firewalls as long as there is a TCP port forwarding to it.
  Device 44 receives BLINK packets on the SWBB bus and replies back to the sender, device 45, thinking it is on the same bus. The LED flashes to indicate each reception.
  The surrogate forwards packets transparently in both directions between buses, pretending to other devices on the SWBB bus to be device 45.
  RemoteWorker on an Uno with Ethernet Shield
  LAN/WAN
  PJON\examples\ARDUINO\Local\EthernetTCP\SoftwareBitBangSurrogate\RemoteWorker\Transmitter
  PJON\examples\ARDUINO\Local\EthernetTCP\SoftwareBitBangSurrogate\Surrogate
  PJON\examples\ARDUINO\Local\SoftwareBitBang\BlinkWithResponse\Receiver
  Remember to change Ethernet settings in RemoteWorker and Surrogate to match YOUR network address, unless connecting them directly!
  This will typically be in a range like 192.168.x.x or 10.x.x.x
