# Fritzing sketch BlinkingRGBSwitch (saved by Fritzing 0.9.3b)

parts:
  Part2 = Arduino Ethernet Shield (Rev3)
  Part4 = Arduino Uno (Rev3) - ICSP  # not connected
  R1 = Resistor [tolerance=±5% resistance=8.2k package=THT]
  R2 = Resistor [tolerance=±5% resistance=33k package=THT]
  R3 = Resistor [tolerance=±5% resistance=23.3k package=THT]
  LED1 = RGB LED - (4 legs) [package="5 mm [THT]"]

nets:
  N1: Part2.GND, LED1.green_cathode
  N2: Part2.SDCS, R3.Pin_0
  N3: Part2.PWM_D5, R2.Pin_0
  N4: Part2.PWM_D6, R1.Pin_0

notes:
  BlinkingRGBSwitch.ino on Uno+Ethernet
  Common cathode RGB LED
  Blinking RGB Switch, LUDP <-> SWBB
  PJON SWBB bus
